// Logisim project ALU.circ as structural Verilog: 1 circuit, main circuit main
module main (
  input  ZX,
  input  NX,
  input  ZY,
  input  NY,
  input  F,
  input  NO,
  input  [15:0] X,
  input  [15:0] Y,
  output [15:0] X_2
);

  wire [15:1] undriven;

  // AND_Gate and_1 has open pins: in0={undriven, ZX}, in1=X, out=open
  // Pins of 1 and 16 bits meet at {undriven, ZX}
endmodule
