// Logisim project Bit.circ as structural Verilog: 1 circuit, main circuit Bit
module Bit (
  input  load,
  input  in,
  output out_3
);

  wire multiplexer_1_out;

  Multiplexer #(.enable("false")) multiplexer_1 (.in0(out_3), .in1(in), .out(multiplexer_1_out), .sel(load));
  D_Flip_Flop #(.trigger("high")) d_ff_1 (.clk(load), .D(multiplexer_1_out), .Q(out_3));  // open: Qn, preset, en, reset
endmodule
