// Logisim project RAM8.circ as structural Verilog: 1 circuit, main circuit RAM8
module RAM8 (
  input  load,
  input  [2:0] addres,
  input  [15:0] in,
  output [15:0] out
);

  wire and_1_out, and_2_out, and_3_out, and_4_out, and_5_out, and_6_out, and_7_out, and_8_out,
       demultiplexer_1_out0, demultiplexer_1_out1, demultiplexer_1_out2, demultiplexer_1_out3,
       demultiplexer_1_out4, demultiplexer_1_out5, demultiplexer_1_out6, demultiplexer_1_out7;
  wire [15:0] register_1_out, register_2_out, register_3_out, register_4_out, register_5_out, register_6_out,
       register_7_out, register_8_out;

  Demultiplexer #(.select(3), .enable("false")) demultiplexer_1 (
    .out0(demultiplexer_1_out0), .out1(demultiplexer_1_out1), .out2(demultiplexer_1_out2),
    .out3(demultiplexer_1_out3), .out4(demultiplexer_1_out4), .out5(demultiplexer_1_out5),
    .out6(demultiplexer_1_out6), .out7(demultiplexer_1_out7), .in(1'b1), .sel(addres));
  and and_1 (and_1_out, demultiplexer_1_out0, load);
  and and_2 (and_2_out, demultiplexer_1_out1, load);
  and and_3 (and_3_out, demultiplexer_1_out2, load);
  and and_4 (and_4_out, demultiplexer_1_out3, load);
  and and_5 (and_5_out, demultiplexer_1_out4, load);
  and and_6 (and_6_out, demultiplexer_1_out5, load);
  and and_7 (and_7_out, demultiplexer_1_out6, load);
  and and_8 (and_8_out, demultiplexer_1_out7, load);
  Register register_1 (.in(in), .load(and_1_out), .out(register_1_out));
  Register register_2 (.in(in), .load(and_2_out), .out(register_2_out));
  Register register_3 (.in(in), .load(and_3_out), .out(register_3_out));
  Register register_4 (.in(in), .load(and_4_out), .out(register_4_out));
  Register register_5 (.in(in), .load(and_5_out), .out(register_5_out));
  Register register_6 (.in(in), .load(and_6_out), .out(register_6_out));
  Register register_7 (.in(in), .load(and_7_out), .out(register_7_out));
  Register register_8 (.in(in), .load(and_8_out), .out(register_8_out));
  Multiplexer #(.select(3), .width(16), .enable("false")) multiplexer_1 (
    .in0(register_1_out), .in1(register_2_out), .in2(register_3_out), .in3(register_4_out),
    .in4(register_5_out), .in5(register_6_out), .in6(register_7_out), .in7(register_8_out), .out(out),
    .sel(addres));
endmodule
