// Logisim project CPU.circ as structural Verilog: 1 circuit, main circuit CPU
module CPU (
  input  [15:0] instruction,
  input  [15:0] inM
);

  wire [15:0] D_out, multiplexer_1_out, multiplexer_2_out, undriven;

  Multiplexer #(.width(16), .enable("false")) multiplexer_1 (
    .in0(instruction), .in1(undriven), .out(multiplexer_1_out), .sel(instruction[15]));
  Register A (.in(multiplexer_1_out));  // open: load, out
  Register D (.in(undriven), .out(D_out));  // open: load
  Multiplexer #(.width(16), .enable("false")) multiplexer_2 (
    .in0(instruction), .in1(inM), .out(multiplexer_2_out), .sel(instruction[15]));
  ALU alu_1 (
    .X(D_out), .Y(multiplexer_2_out), .ZX(instruction[11]), .NX(instruction[10]), .ZY(instruction[9]),
    .NY(instruction[8]), .F(instruction[7]), .NO(instruction[6]));  // open: OUT, ZR, NG
endmodule
